# Fritzing sketch 110519018 (saved by Fritzing 0.9.3b)
breadboards: 1

parts:
  元件2 = Arduino Uno (Rev3)
  R1 = Resistor [tolerance=±5% resistance=220 package=THT]
  R4 = Resistor [tolerance=±5% resistance=220 package=THT]
  R5 = Resistor [tolerance=±5% resistance=220 package=THT]
  D1 = LED_BARGRAPH_10 [package=led_bargaph_10]
  J1 = Basic Force Sensing Resistor (FSR) [package=THT]
  元件1 = OLED Monochrome 128x64 0.96 inch [part_number=326]
  R12 = Resistor [tolerance=±5% resistance=220 package=THT]
  R13 = Resistor [tolerance=±5% resistance=220 package=THT]
  R14 = Resistor [tolerance=±5% resistance=220 package=THT]
  R15 = Resistor [tolerance=±5% resistance=220 package=THT]
  R16 = Resistor [tolerance=±5% resistance=220 package=THT]
  R17 = Resistor [tolerance=±5% resistance=220 package=THT]
  R18 = Resistor [tolerance=±5% resistance=220 package=THT]
  R19 = Resistor [tolerance=±5% resistance=220 package=THT]

nets:
  N1: 元件2.A0, R5.Pin_0, J1.pin_1
  N2: 元件2.D8, D1.D_C, 元件1.CS, R18.Pin_1
  N3: 元件2.D9_PWM, D1.C_C, 元件1.DC_SA0, R17.Pin_1
  N4: 元件2.D10_PWM/SS, D1.B_C, 元件1.RESET, R16.Pin_1
  N5: 元件2.D11_PWM/MOSI, D1.A_C, 元件1.SCLK_SCK, R15.Pin_1
  N6: 元件2.D12/MISO, 元件1.MOSI_SDA
  N7: 元件2.D2, R1.Pin_1, D1.J_C
  N8: 元件2.D3_PWM, D1.I_C, R12.Pin_1
  N9: 元件2.D4, D1.H_C, R13.Pin_1
  N10: 元件2.D5_PWM, D1.G_C, R14.Pin_1
  N11: 元件2.D6_PWM, R4.Pin_0, D1.F_C
  N12: 元件2.D7, D1.E_C, R19.Pin_1
  5V: 元件2.5V, J1.pin_0, 元件1.VIN
  N13: 元件2.GND, R5.Pin_1
  N14: R1.Pin_0, R4.Pin_1, 元件1.GND, R12.Pin_0, R13.Pin_0, R14.Pin_0, R15.Pin_0, R16.Pin_0, R17.Pin_0, R18.Pin_0, R19.Pin_0

custom parts:
  OLED Monochrome 128x64 0.96 inch: These displays are small, only about 1" diameter, but very readable due to the high contrast of an OLED display. This display is made of 128x64 individual white OLED pixels, each one is turned on or off by the controller chip. Because the display makes its own light, no backlight is required. This reduces the power required to run the OLED and is why the display has such high contrast; we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
